# Fritzing sketch Modelo (saved by Fritzing 0.9.2b)

parts:
  Mod1 = ESP32 - CAM
  Componente1 = Arduino Uno (Rev3)
  Mod2 = ESP32 - CAM
  Componente2 = LCD1602-I2C

nets:
  5V: Mod1.5V, Componente1.5V
  GND: Mod1.GND, Componente1.GND
  N1: Mod1.VOT, Componente1.D1/TX
  N2: Mod1.VOR, Componente1.D0/RX
  GND_2: Mod2.GND, Componente2.GND
  N3: Mod2.IO13, Componente2.SCL
  N4: Mod2.IO2, Componente2.SDA
  VCC: Mod2.VCC, Componente2.VCC

notes:
  PARA PROGRAMAÇÃO
  PARA O USO FINAL
  5V
  GND

custom parts:
  ESP32 - CAM: The ESP32-CAM has a very competitive small-size camera module that can operate independently as a minimum system with a footprint of only 27*40.5*4.5mm and a deep sleep current of up to 6mA.
  LCD1602-I2C: A standard character display, usually with 2x16 characters. Comes in many colors with LCM1602 IIC attached.
